// Logisim project PROJECT (1).circ as structural Verilog: 10 circuits, main circuit main
module main (
);

  wire BTN_DOWN, BTN_LEFT, BTN_RES, BTN_RIGHT, BTN_UP, DOWN_out, EV_BONUS_PICKUP, EV_EXIT_REACHED,
       EV_KEY_PICKUP, EV_PLAYER_MOVE, EV_TRAP_TRIGGER, LEFT_out, LOAD_X, LOAD_Y, RESET, RIGHT_out, TACTS,
       UP_out, WE_MAP;
  wire [3:0] CELL_TYPE, SCAN_Q;
  wire [4:0] NEW_Y, POS_Y;
  wire [5:0] NEW_X, POS_X;
  wire [10:0] ADDR, ADDR_NEXT;

  Clock clock_1 (.out(TACTS));
  Button RIGHT (.out(RIGHT_out));
  Button LEFT (.out(LEFT_out));
  Button UP (.out(UP_out));
  Button DOWN (.out(DOWN_out));
  Button u_RESET (.out(RESET));
  BTN_INPUT btn_input_1 (
    .TACT(TACTS), .RIGHT(RIGHT_out), .LEFT(LEFT_out), .UP(UP_out), .DOWN(DOWN_out), .RESET(RESET),
    .B_RIGHT(BTN_RIGHT), .B_LEFT(BTN_LEFT), .B_UP(BTN_UP), .B_DOWN(BTN_DOWN), .B_RESET(BTN_RES));
  MOVE_LOGIC move_logic_1 (
    .POS_Y(POS_Y), .POS_X(POS_X), .CELL_TYPE(CELL_TYPE), .MOVE_ENABLE(1'b1), .GAME_STATE(2'b00),
    .B_RIGHT(BTN_RIGHT), .B_LEFT(BTN_LEFT), .EXIT_OPEN(1'b0), .B_UP(BTN_UP), .B_DOWN(BTN_DOWN),
    .ADDR_NEXT(ADDR_NEXT), .NEW_X(NEW_X), .NEW_Y(NEW_Y), .EV_KEY_PICKUP(EV_KEY_PICKUP),
    .EV_TRAP_TRIGGER(EV_TRAP_TRIGGER), .EV_BONUS_PICKUP(EV_BONUS_PICKUP), .LOAD_X(LOAD_X),
    .EV_EXIT_REACHED(EV_EXIT_REACHED), .EV_PLAYER_MOVE(EV_PLAYER_MOVE), .LOAD_Y(LOAD_Y), .WE_MAP(WE_MAP));
  PLAYER_POS player_pos_1 (
    .NEW_X(NEW_X), .NEW_Y(NEW_Y), .LOAD_X(LOAD_X), .RESET_3(RESET), .LOAD_Y(LOAD_Y), .POS_X(POS_X),
    .RESET(BTN_RES), .RESET_2(BTN_RES), .TACT(TACTS), .TACT_2(TACTS), .POS_Y(POS_Y), .ADDR(ADDR));
  MAP_MEM map_mem_1 (.ADDR(ADDR), .WE(WE_MAP), .TACT(TACTS), .SCAN_Q(SCAN_Q), .CELL_TYPE(CELL_TYPE));
endmodule

module BTN_INPUT (
  input  TACT,
  input  RIGHT,
  input  LEFT,
  input  UP,
  input  DOWN,
  input  RESET,
  output B_RIGHT,
  output B_LEFT,
  output B_UP,
  output B_DOWN,
  output B_RESET
);

  wire d_ff_1_q, d_ff_2_q, d_ff_3_q, d_ff_4_q, not_1_out, not_2_out, not_3_out, not_4_out;

  D_Flip_Flop d_ff_1 (.clk(TACT), .D(RIGHT), .Q(d_ff_1_q));  // open: Qn, preset, en, reset
  D_Flip_Flop d_ff_2 (.clk(TACT), .D(LEFT), .Q(d_ff_2_q));  // open: Qn, preset, en, reset
  D_Flip_Flop d_ff_3 (.clk(TACT), .D(UP), .Q(d_ff_3_q));  // open: Qn, preset, en, reset
  D_Flip_Flop d_ff_4 (.clk(TACT), .D(DOWN), .Q(d_ff_4_q));  // open: Qn, preset, en, reset
  not not_1 (not_1_out, d_ff_1_q);
  not not_2 (not_2_out, d_ff_2_q);
  not not_3 (not_3_out, d_ff_3_q);
  not not_4 (not_4_out, d_ff_4_q);
  and and_1 (B_RIGHT, not_1_out, RIGHT);
  and and_2 (B_LEFT, not_2_out, LEFT);
  and and_3 (B_UP, not_3_out, UP);
  and and_4 (B_DOWN, not_4_out, DOWN);

  assign B_RESET = RESET;
endmodule

module PLAYER_POS (
  input  [5:0] NEW_X,
  input  RESET,
  input  TACT,
  input  [4:0] NEW_Y,
  input  RESET_2,
  input  TACT_2,
  input  LOAD_X,
  input  RESET_3,
  input  LOAD_Y,
  output [5:0] POS_X,
  output [10:0] ADDR,
  output [4:0] POS_Y
);

  wire LOAD_X_OR_RESET, LOAD_Y_OR_RESET;
  wire [4:0] multiplexer_2_out;
  wire [5:0] multiplexer_1_out;

  or or_1 (LOAD_X_OR_RESET, LOAD_X, RESET_3);
  or or_2 (LOAD_Y_OR_RESET, RESET_3, LOAD_Y);
  Multiplexer #(.width(6), .enable("false")) multiplexer_1 (
    .in0(NEW_X), .in1(6'b000010), .out(multiplexer_1_out), .sel(RESET));
  Multiplexer #(.width(5), .enable("false")) multiplexer_2 (
    .in0(NEW_Y), .in1(5'b00010), .out(multiplexer_2_out), .sel(RESET_2));
  Register #(.width(6)) u_POS_X (.D(multiplexer_1_out), .en(LOAD_X_OR_RESET), .Q(ADDR[5:0]), .clk(TACT));  // open: clr
  Register #(.width(5)) u_POS_Y (
    .D(multiplexer_2_out), .en(LOAD_Y_OR_RESET), .Q(ADDR[10:6]), .clk(TACT_2));  // open: clr

  assign POS_X = ADDR[5:0];
  assign POS_Y = ADDR[10:6];

  // Notes on the sheet:
  //   START_X
  //   START_Y
endmodule

module MAP_MEM (
  input  [10:0] ADDR,
  input  WE,
  input  TACT,
  output [3:0] CELL_TYPE,
  output [3:0] SCAN_Q
);

  RAM #(.addrWidth(11), .dataWidth(4), .bus("separate")) ram_1 (
    .addr(ADDR), .din(4'b0000), .data(CELL_TYPE), .str(WE), .sel(1'b1), .clk(TACT), .ld(1'b1), .clr(1'b0));
  RAM #(.addrWidth(12), .dataWidth(4)) ram_2 ();  // open: addr, data, sel, clk, ld, clr
  Counter counter_1 ();  // open: load, D, count, Q, carry, clk, clr

  assign SCAN_Q = CELL_TYPE;

  // Notes on the sheet:
  //   MAP_DATA_BACKUP
  //   MAP_DATA
endmodule

module RESET (
  input  TACT
);
endmodule

module MOVE_LOGIC (
  input  [4:0] POS_Y,
  input  [5:0] POS_X,
  input  [3:0] CELL_TYPE,
  input  MOVE_ENABLE,
  input  [1:0] GAME_STATE,
  input  B_RIGHT,
  input  B_LEFT,
  input  EXIT_OPEN,
  input  B_UP,
  input  B_DOWN,
  output [10:0] ADDR_NEXT,
  output [5:0] NEW_X,
  output [4:0] NEW_Y,
  output EV_KEY_PICKUP,
  output EV_TRAP_TRIGGER,
  output EV_BONUS_PICKUP,
  output LOAD_X,
  output EV_EXIT_REACHED,
  output EV_PLAYER_MOVE,
  output LOAD_Y,
  output WE_MAP
);

  wire ALLOWED, and_10_out, CAN_ENTER, comparator_2_eq, comparator_3_gt, comparator_4_gt, comparator_5_eq,
       DO_D, DO_L, DO_R, DO_U, DOWN_OK, GANE_ACTIVE, IS_BONUS, IS_EXIT_C, IS_EXIT_O, IS_KEY, IS_PASS,
       IS_START, IS_TRAP, IS_WALL, LEFT_OK, not_1_out, or_8_out, RIGHT_OK, SAFE_D, SAFE_L, SAFE_R, SAFE_U,
       UP_OK;
  wire [1:0] or_4_out;
  wire [4:0] NEW_Y_D, NEW_Y_U;
  wire [5:0] NEW_X_L, NEW_X_R;

  Decoder #(.select(4), .enable("false")) decoder_1 (
    .out0(IS_PASS), .out1(IS_WALL), .out2(IS_KEY), .out3(IS_EXIT_C), .out4(IS_EXIT_O), .out5(IS_TRAP),
    .out6(IS_BONUS), .out7(IS_START), .sel(CELL_TYPE));  // open: out8, out9, out10, out11, out12, out13, out14, out15
  Comparator #(.width(2)) comparator_1 (.a(GAME_STATE), .b(2'b00), .eq(GANE_ACTIVE));  // open: gt, lt
  Adder #(.width(5)) adder_1 (.a(POS_Y), .b(5'b00001), .out(NEW_Y_U));  // open: cin, cout
  Adder #(.width(6)) adder_2 (.a(POS_X), .b({6{1'b0}}), .out(NEW_X_R));  // open: cin, cout
  Subtractor #(.width(5)) subtractor_1 (.a(POS_Y), .b(5'b11110), .out(NEW_Y_D));  // open: bin, bout
  Subtractor #(.width(6)) subtractor_2 (.a(POS_X), .b({6{1'b0}}), .out(NEW_X_L));  // open: bin, bout
  Comparator #(.width(5), .mode("unsigned")) comparator_2 (
    .a(POS_Y), .b({5{1'b0}}), .eq(comparator_2_eq));  // open: gt, lt
  Comparator #(.width(6), .mode("unsigned")) comparator_3 (
    .a(NEW_X_R), .b(6'b111110), .gt(comparator_3_gt));  // open: eq, lt
  Comparator #(.width(5), .mode("unsigned")) comparator_4 (
    .a(NEW_Y_D), .b({5{1'b0}}), .gt(comparator_4_gt));  // open: eq, lt
  Comparator #(.width(6), .mode("unsigned")) comparator_5 (
    .a(POS_X), .b({6{1'b0}}), .eq(comparator_5_eq));  // open: gt, lt
  and and_1 (ALLOWED, GANE_ACTIVE, MOVE_ENABLE);
  and and_2 (RIGHT_OK, B_RIGHT, MOVE_ENABLE);
  and and_3 (LEFT_OK, B_LEFT, MOVE_ENABLE);
  and and_4 (UP_OK, B_UP, MOVE_ENABLE);
  and and_5 (DOWN_OK, B_DOWN, MOVE_ENABLE);
  not not_1 (not_1_out, comparator_5_eq);
  not not_2 (SAFE_U, comparator_2_eq);
  not not_3 (SAFE_R, comparator_3_gt);
  not not_4 (SAFE_D, comparator_4_gt);
  not not_5 (SAFE_L, not_1_out);
  or or_1 (CAN_ENTER, IS_PASS, IS_KEY, IS_EXIT_O, IS_TRAP, IS_BONUS, IS_START);
  Multiplexer #(.select(2), .width(11), .enable("false")) multiplexer_1 (
    .in0({POS_Y, NEW_X_R}), .in1({POS_Y, NEW_X_L}), .in2({NEW_Y_D, POS_X}), .in3({NEW_Y_U, POS_X}),
    .out(ADDR_NEXT), .sel(or_4_out));
  and and_6 (DO_R, RIGHT_OK, SAFE_R, CAN_ENTER);
  and and_7 (DO_L, LEFT_OK, SAFE_L, CAN_ENTER);
  and and_8 (DO_U, UP_OK, SAFE_U, CAN_ENTER);
  and and_9 (DO_D, DOWN_OK, SAFE_D, CAN_ENTER);
  or or_2 (LOAD_X, DO_R, DO_L);
  or or_3 (LOAD_Y, DO_U, DO_D);
  or or_4 (or_4_out[0], LEFT_OK, UP_OK);
  or or_5 (or_4_out[1], DOWN_OK, UP_OK);
  Multiplexer #(.width(6), .enable("false")) multiplexer_2 (.in0(NEW_X_R), .in1(NEW_X_L), .out(NEW_X), .sel(DO_L));
  Multiplexer #(.width(5), .enable("false")) multiplexer_3 (.in0(NEW_Y_D), .in1(NEW_Y_U), .out(NEW_Y), .sel(DO_U));
  and and_10 (and_10_out, IS_EXIT_C, EXIT_OPEN);
  or or_6 (WE_MAP, EV_KEY_PICKUP, EV_BONUS_PICKUP);
  or or_7 (EV_PLAYER_MOVE, DO_R, DO_L, DO_U, DO_D);
  and and_11 (EV_KEY_PICKUP, EV_PLAYER_MOVE, IS_KEY);
  and and_12 (EV_TRAP_TRIGGER, EV_PLAYER_MOVE, IS_TRAP);
  and and_13 (EV_BONUS_PICKUP, EV_PLAYER_MOVE, IS_BONUS);
  or or_8 (or_8_out, and_10_out, IS_EXIT_O);
  and and_14 (EV_EXIT_REACHED, EV_PLAYER_MOVE, or_8_out);
  BitSelector bitselector_1 ();  // open: in, out, sel

  // Other names for the same wires on the sheet: ANY_MOVE = EV_PLAYER_MOVE

  // Notes on the sheet:
  //   UP
  //   RIGHT
  //   DOWN
  //   LEFT
  //   RIGHT
  //   LEFT
  //   DOWN
  //   UP
  //   DO RLUD
endmodule

module DISPLAY (
  input  TACT,
  input  [5:0] POS_X,
  input  [4:0] POS_Y,
  input  [4:0] in_4,
  input  [6:0] in_5,
  input  [3:0] MAP_Q,
  output [10:0] SCAN_ADDR
);

  wire _0, _1, _2, _3, _4, _5, _6, _7, _8, _9, _10, _11, _12, _13, _14, _15, _16, _17, _18, _19, _20, _21,
       _22, _23, _24, _25, _26, _27, _28, _29, _30, _31, comparator_2_eq, comparator_3_eq, decoder_1_out1,
       decoder_1_out2, decoder_1_out3, decoder_1_out4, decoder_1_out5, decoder_1_out6, decoder_1_out7,
       FINAL_PIXEL, IS_PLAYER, MAP_PIXEL, ROW_READY, SCAN_X_carry, TACT_t, undriven, WRITE_EN;
  wire [4:0] SCAN_X;
  wire [5:0] OFFSET_X;
  wire [31:0] RD, REG_0, REG_1, REG_2, REG_3, REG_4, REG_5, REG_6, REG_7, REG_8, REG_9, REG_10, REG_11,
       REG_12, REG_13, REG_14, REG_15, REG_16, REG_17, REG_18, REG_19, REG_20, REG_21, REG_22, REG_23,
       REG_24, REG_25, REG_26, REG_27, REG_28, REG_29, REG_30, REG_31;

  Decoder #(.select(4), .enable("false")) decoder_1 (
    .out1(decoder_1_out1), .out2(decoder_1_out2), .out3(decoder_1_out3), .out4(decoder_1_out4),
    .out5(decoder_1_out5), .out6(decoder_1_out6), .out7(decoder_1_out7), .sel(MAP_Q));  // open: out0, out8, out9, out10, out11, out12, out13, out14, out15
  Clock clock_1 (.out(TACT_t));
  or or_1 (MAP_PIXEL, decoder_1_out1, decoder_1_out2, decoder_1_out3, decoder_1_out4, decoder_1_out5, decoder_1_out6, decoder_1_out7);
  Comparator #(.width(5)) comparator_1 (.a(SCAN_X), .b({5{1'b1}}), .eq(ROW_READY));  // open: gt, lt
  RESET reset_1 ();  // open: TACT
  Counter #(.width(5), .max('h1f)) u_SCAN_X (
    .Q(SCAN_X), .carry(SCAN_X_carry), .clk(TACT_t));  // open: load, D, count, clr
  Multiplexer #(.width(6), .enable("false")) multiplexer_1 (
    .in0({6{1'b0}}), .in1(6'b110010), .out(OFFSET_X), .sel(POS_X[5]));
  Counter #(.width(5), .max('h1f)) SCAN_Y (
    .Q(SCAN_ADDR[10:6]), .clk(SCAN_X_carry));  // open: load, D, count, carry, clr
  or or_2 (FINAL_PIXEL, MAP_PIXEL, IS_PLAYER);
  Demultiplexer #(.select(5), .enable("false")) demultiplexer_1 (
    .out0(_0), .out1(_1), .out2(_2), .out3(_3), .out4(_4), .out5(_5), .out6(_6), .out7(_7), .out8(_8),
    .out9(_9), .out10(_10), .out11(_11), .out12(_12), .out13(_13), .out14(_14), .out15(_15), .out16(_16),
    .out17(_17), .out18(_18), .out19(_19), .out20(_20), .out21(_21), .out22(_22), .out23(_23), .out24(_24),
    .out25(_25), .out26(_26), .out27(_27), .out28(_28), .out29(_29), .out30(_30), .out31(_31),
    .in(ROW_READY), .sel(SCAN_ADDR[10:6]));
  Adder #(.width(6)) adder_1 (.a(OFFSET_X), .b({1'b0, SCAN_X}), .out(SCAN_ADDR[5:0]));  // open: cin, cout
  Comparator #(.width(5)) comparator_2 (.a(SCAN_X), .b(POS_X[4:0]), .eq(comparator_2_eq));  // open: gt, lt
  Comparator #(.width(5)) comparator_3 (.a(SCAN_ADDR[10:6]), .b(POS_Y), .eq(comparator_3_eq));  // open: gt, lt
  and and_1 (IS_PLAYER, comparator_2_eq, comparator_3_eq);
  Register #(.width(32)) register_1 (.D(RD), .en(_0), .Q(REG_0), .clk(TACT_t));  // open: clr
  Register #(.width(32)) register_2 (.D(RD), .en(_8), .Q(REG_8), .clk(TACT_t));  // open: clr
  Register #(.width(32)) register_3 (.D(RD), .en(_16), .Q(REG_16), .clk(TACT_t));  // open: clr
  Register #(.width(32)) register_4 (.D(RD), .en(_24), .Q(REG_24), .clk(TACT_t));  // open: clr
  Shift_Register #(.length(32)) shift_register_1 (
    .shift(undriven), .in(FINAL_PIXEL), .clk(TACT_t), .d0(_0), .q0(RD[0]), .d1(_1), .q1(RD[1]), .d2(_2),
    .q2(RD[2]), .d3(_3), .q3(RD[3]), .d4(_4), .q4(RD[4]), .d5(_5), .q5(RD[5]), .d6(_6), .q6(RD[6]), .d7(_7),
    .q7(RD[7]), .d8(_8), .q8(RD[8]), .d9(_9), .q9(RD[9]), .d10(_10), .q10(RD[10]), .d11(_11), .q11(RD[11]),
    .d12(_12), .q12(RD[12]), .d13(_13), .q13(RD[13]), .d14(_14), .q14(RD[14]), .d15(_15), .q15(RD[15]),
    .d16(_16), .q16(RD[16]), .d17(_17), .q17(RD[17]), .d18(_18), .q18(RD[18]), .d19(_19), .q19(RD[19]),
    .d20(_20), .q20(RD[20]), .d21(_21), .q21(RD[21]), .d22(_22), .q22(RD[22]), .d23(_23), .q23(RD[23]),
    .d24(_24), .q24(RD[24]), .d25(_25), .q25(RD[25]), .d26(_26), .q26(RD[26]), .d27(_27), .q27(RD[27]),
    .d28(_28), .q28(RD[28]), .d29(_29), .q29(RD[29]), .d30(_30), .q30(RD[30]), .d31(_31), .q31(RD[31]));  // open: out, load, clr
  Register #(.width(32)) register_5 (.D(RD), .en(_1), .Q(REG_1), .clk(TACT_t));  // open: clr
  Register #(.width(32)) register_6 (.D(RD), .en(_9), .Q(REG_9), .clk(TACT_t));  // open: clr
  Register #(.width(32)) register_7 (.D(RD), .en(_17), .Q(REG_17), .clk(TACT_t));  // open: clr
  Register #(.width(32)) register_8 (.D(RD), .en(_25), .Q(REG_25), .clk(TACT_t));  // open: clr
  Comparator #(.width(5)) comparator_4 (.a(SCAN_X), .b({5{1'b1}}), .eq(WRITE_EN));  // open: gt, lt
  Register #(.width(32)) register_9 (.D(RD), .en(_2), .Q(REG_2), .clk(TACT_t));  // open: clr
  Register #(.width(32)) register_10 (.D(RD), .en(_10), .Q(REG_10), .clk(TACT_t));  // open: clr
  Register #(.width(32)) register_11 (.D(RD), .en(_18), .Q(REG_18), .clk(TACT_t));  // open: clr
  Register #(.width(32)) register_12 (.D(RD), .en(_26), .Q(REG_26), .clk(TACT_t));  // open: clr
  DotMatrix #(.matrixcols(32), .matrixrows(32)) dotmatrix_1 (
    .col0(REG_0), .col1(REG_1), .col2(REG_2), .col3(REG_3), .col4(REG_4), .col5(REG_5), .col6(REG_6),
    .col7(REG_7), .col8(REG_8), .col9(REG_9), .col10(REG_10), .col11(REG_11), .col12(REG_12), .col13(REG_13),
    .col14(REG_14), .col15(REG_15), .col16(REG_16), .col17(REG_17), .col18(REG_18), .col19(REG_19),
    .col20(REG_20), .col21(REG_21), .col22(REG_22), .col23(REG_23), .col24(REG_24), .col25(REG_25),
    .col26(REG_26), .col27(REG_27), .col28(REG_28), .col29(REG_29), .col30(REG_30), .col31(REG_31));
  Register #(.width(32)) register_13 (.D(RD), .en(_3), .Q(REG_3), .clk(TACT_t));  // open: clr
  Register #(.width(32)) register_14 (.D(RD), .en(_11), .Q(REG_11), .clk(TACT_t));  // open: clr
  Register #(.width(32)) register_15 (.D(RD), .en(_19), .Q(REG_19), .clk(TACT_t));  // open: clr
  Register #(.width(32)) register_16 (.D(RD), .en(_27), .Q(REG_27), .clk(TACT_t));  // open: clr
  Register #(.width(32)) register_17 (.D(RD), .en(_4), .Q(REG_4), .clk(TACT_t));  // open: clr
  Register #(.width(32)) register_18 (.D(RD), .en(_12), .Q(REG_12), .clk(TACT_t));  // open: clr
  Register #(.width(32)) register_19 (.D(RD), .en(_20), .Q(REG_20), .clk(TACT_t));  // open: clr
  Register #(.width(32)) register_20 (.D(RD), .en(_28), .Q(REG_28), .clk(TACT_t));  // open: clr
  Register #(.width(32)) register_21 (.D(RD), .en(_5), .Q(REG_5), .clk(TACT_t));  // open: clr
  Register #(.width(32)) register_22 (.D(RD), .en(_13), .Q(REG_13), .clk(TACT_t));  // open: clr
  Register #(.width(32)) register_23 (.D(RD), .en(_21), .Q(REG_21), .clk(TACT_t));  // open: clr
  Register #(.width(32)) register_24 (.D(RD), .en(_29), .Q(REG_29), .clk(TACT_t));  // open: clr
  DotMatrix #(.inputtype("row"), .matrixcols(32), .matrixrows(32)) dotmatrix_2 (
    .row0(REG_0), .row1(REG_1), .row2(REG_2), .row3(REG_3), .row4(REG_4), .row5(REG_5), .row6(REG_6),
    .row7(REG_7), .row8(REG_8), .row9(REG_9), .row10(REG_10), .row11(REG_11), .row12(REG_12), .row13(REG_13),
    .row14(REG_14), .row15(REG_15), .row16(REG_16), .row17(REG_17), .row18(REG_18), .row19(REG_19),
    .row20(REG_20), .row21(REG_21), .row22(REG_22), .row23(REG_23), .row24(REG_24), .row25(REG_25),
    .row26(REG_26), .row27(REG_27), .row28(REG_28), .row29(REG_29), .row30(REG_30), .row31(REG_31));
  Register #(.width(32)) register_25 (.D(RD), .en(_6), .Q(REG_6), .clk(TACT_t));  // open: clr
  Register #(.width(32)) register_26 (.D(RD), .en(_14), .Q(REG_14), .clk(TACT_t));  // open: clr
  Register #(.width(32)) register_27 (.D(RD), .en(_22), .Q(REG_22), .clk(TACT_t));  // open: clr
  Register #(.width(32)) register_28 (.D(RD), .en(_30), .Q(REG_30), .clk(TACT_t));  // open: clr
  Register #(.width(32)) register_29 (.D(RD), .en(_7), .Q(REG_7), .clk(TACT_t));  // open: clr
  Register #(.width(32)) register_30 (.D(RD), .en(_15), .Q(REG_15), .clk(TACT_t));  // open: clr
  Register #(.width(32)) register_31 (.D(RD), .en(_23), .Q(REG_23), .clk(TACT_t));  // open: clr
  Register #(.width(32)) register_32 (.D(RD), .en(_31), .Q(REG_31), .clk(TACT_t));  // open: clr

  // Other names for the same wires on the sheet: BLOCK_SEL = POS_X[5]; REAL_X[5:0] = SCAN_ADDR[5:0];
  //   SCAN_Y[4:0] = SCAN_ADDR[10:6]
endmodule

module GAME_SCREEN (
  input  [1:0] in_1,
  input  [28:0] in_2,
  input  [28:0] in_3,
  input  [28:0] in_4,
  input  [28:0] in_5,
  input  [28:0] in_6,
  input  [28:0] in_7,
  input  [28:0] in_8,
  input  [28:0] in_9,
  input  [28:0] in_10,
  input  [28:0] in_11,
  input  [28:0] in_12,
  input  [28:0] in_13,
  input  [28:0] in_14,
  input  [28:0] in_15,
  input  [28:0] in_16,
  input  [28:0] in_17,
  input  [28:0] in_18,
  input  [28:0] in_19,
  input  [28:0] in_20,
  input  [28:0] in_21,
  input  [28:0] in_22,
  input  [28:0] in_23,
  input  [28:0] in_24,
  input  [28:0] in_25,
  input  [28:0] in_26,
  input  [28:0] in_27,
  input  [28:0] in_28,
  input  [28:0] in_29,
  input  [28:0] in_30,
  input  [28:0] in_31,
  input  [28:0] in_32,
  input  [28:0] in_33,
  output [28:0] out_34,
  output [28:0] out_35,
  output [28:0] out_36,
  output [28:0] out_37,
  output [28:0] out_38,
  output [28:0] out_39,
  output [28:0] out_40,
  output [28:0] out_41,
  output [28:0] out_42,
  output [28:0] out_43,
  output [28:0] out_44,
  output [28:0] out_45,
  output [28:0] out_46,
  output [28:0] out_47,
  output [28:0] out_48,
  output [28:0] out_49,
  output [28:0] out_50,
  output [28:0] out_51,
  output [28:0] out_52,
  output [28:0] out_53,
  output [28:0] out_54,
  output [28:0] out_55,
  output [28:0] out_56,
  output [28:0] out_57,
  output [28:0] out_58,
  output [28:0] out_59,
  output [28:0] out_60,
  output [28:0] out_61,
  output [28:0] out_62,
  output [28:0] out_63,
  output [28:0] out_64,
  output [28:0] out_65
);

  Multiplexer #(.select(2), .width(29), .enable("false")) multiplexer_1 (
    .in0(in_2), .in1({29{1'b0}}), .in2({29{1'b0}}), .in3({29{1'b0}}), .out(out_34), .sel(in_1));
  Multiplexer #(.select(2), .width(29), .enable("false")) multiplexer_2 (
    .in0(in_13), .in1(29'h3e00fe0), .in2(29'hfe01ff0), .in3({29{1'b0}}), .out(out_35), .sel(in_1));
  Multiplexer #(.select(2), .width(29), .enable("false")) multiplexer_3 (
    .in0(in_24), .in1(29'h7f01010), .in2(29'h101100), .in3({29{1'b0}}), .out(out_36), .sel(in_1));
  Multiplexer #(.select(2), .width(29), .enable("false")) multiplexer_4 (
    .in0(in_3), .in1(29'hc181010), .in2(29'h481100), .in3(29'h6100c20), .out(out_37), .sel(in_1));
  Multiplexer #(.select(2), .width(29), .enable("false")) multiplexer_5 (
    .in0(in_14), .in1(29'h8181010), .in2(29'h81100), .in3(29'h9081210), .out(out_38), .sel(in_1));
  Multiplexer #(.select(2), .width(29), .enable("false")) multiplexer_6 (
    .in0(in_25), .in1(29'h8981010), .in2(29'h481100), .in3(29'h8881110), .out(out_39), .sel(in_1));
  Multiplexer #(.select(2), .width(29), .enable("false")) multiplexer_7 (
    .in0(in_4), .in1(29'hcf00fe0), .in2(29'h100000), .in3(29'h8481090), .out(out_40), .sel(in_1));
  Multiplexer #(.select(2), .width(29), .enable("false")) multiplexer_8 (
    .in0(in_15), .in1(29'h600000), .in2(29'hfe01ff0), .in3(29'h4300860), .out(out_41), .sel(in_1));
  Multiplexer #(.select(2), .width(29), .enable("false")) multiplexer_9 (
    .in0(in_26), .in1({29{1'b0}}), .in2(29'h1180), .in3({29{1'b0}}), .out(out_42), .sel(in_1));
  Multiplexer #(.select(2), .width(29), .enable("false")) multiplexer_10 (
    .in0(in_5), .in1(29'hf81f00), .in2(29'h1140), .in3(29'h8001000), .out(out_43), .sel(in_1));
  Multiplexer #(.select(2), .width(29), .enable("false")) multiplexer_11 (
    .in0(in_16), .in1(29'h3c003c0), .in2(29'h1120), .in3(29'h8001000), .out(out_44), .sel(in_1));
  Multiplexer #(.select(2), .width(29), .enable("false")) multiplexer_12 (
    .in0(in_27), .in1(29'h6400060), .in2(29'hf80e10), .in3(29'h8001000), .out(out_45), .sel(in_1));
  Multiplexer #(.select(2), .width(29), .enable("false")) multiplexer_13 (
    .in0(in_6), .in1(29'hcc00030), .in2(29'h3c00000), .in3(29'hff81ff0), .out(out_46), .sel(in_1));
  Multiplexer #(.select(2), .width(29), .enable("false")) multiplexer_14 (
    .in0(in_17), .in1(29'hcc00030), .in2(29'h647dff0), .in3(29'h8001000), .out(out_47), .sel(in_1));
  Multiplexer #(.select(2), .width(29), .enable("false")) multiplexer_15 (
    .in0(in_28), .in1(29'h6400060), .in2(29'hcc55110), .in3(29'h8001000), .out(out_48), .sel(in_1));
  Multiplexer #(.select(2), .width(29), .enable("false")) multiplexer_16 (
    .in0(in_7), .in1(29'h3c003c0), .in2(29'hcc55110), .in3(29'h8001000), .out(out_49), .sel(in_1));
  Multiplexer #(.select(2), .width(29), .enable("false")) multiplexer_17 (
    .in0(in_18), .in1(29'hf81f00), .in2(29'h6439110), .in3({29{1'b0}}), .out(out_50), .sel(in_1));
  Multiplexer #(.select(2), .width(29), .enable("false")) multiplexer_18 (
    .in0(in_29), .in1({29{1'b0}}), .in2(29'h3c11110), .in3(29'h7f00fe0), .out(out_51), .sel(in_1));
  Multiplexer #(.select(2), .width(29), .enable("false")) multiplexer_19 (
    .in0(in_8), .in1(29'hff80000), .in2(29'hf90000), .in3(29'h8081010), .out(out_52), .sel(in_1));
  Multiplexer #(.select(2), .width(29), .enable("false")) multiplexer_20 (
    .in0(in_19), .in1(29'h4001ff0), .in2(29'h11ff0), .in3(29'h8081010), .out(out_53), .sel(in_1));
  Multiplexer #(.select(2), .width(29), .enable("false")) multiplexer_21 (
    .in0(in_30), .in1(29'h2001110), .in2(29'hff91110), .in3(29'h8081010), .out(out_54), .sel(in_1));
  Multiplexer #(.select(2), .width(29), .enable("false")) multiplexer_22 (
    .in0(in_9), .in1(29'h1001110), .in2(29'h8c19110), .in3(29'h8081010), .out(out_55), .sel(in_1));
  Multiplexer #(.select(2), .width(29), .enable("false")) multiplexer_23 (
    .in0(in_20), .in1(29'h2001110), .in2(29'h8a15110), .in3(29'h7f00fe0), .out(out_56), .sel(in_1));
  Multiplexer #(.select(2), .width(29), .enable("false")) multiplexer_24 (
    .in0(in_31), .in1(29'h4001110), .in2(29'h8919110), .in3({29{1'b0}}), .out(out_57), .sel(in_1));
  Multiplexer #(.select(2), .width(29), .enable("false")) multiplexer_25 (
    .in0(in_10), .in1(29'hff80000), .in2(29'h7080000), .in3(29'hff81ff0), .out(out_58), .sel(in_1));
  Multiplexer #(.select(2), .width(29), .enable("false")) multiplexer_26 (
    .in0(in_21), .in1({29{1'b0}}), .in2({29{1'b0}}), .in3(29'h8801100), .out(out_59), .sel(in_1));
  Multiplexer #(.select(2), .width(29), .enable("false")) multiplexer_27 (
    .in0(in_32), .in1(29'hff81ff0), .in2(29'hff81fd0), .in3(29'h8801100), .out(out_60), .sel(in_1));
  Multiplexer #(.select(2), .width(29), .enable("false")) multiplexer_28 (
    .in0(in_11), .in1(29'h8881180), .in2(29'h8880000), .in3(29'h8801100), .out(out_61), .sel(in_1));
  Multiplexer #(.select(2), .width(29), .enable("false")) multiplexer_29 (
    .in0(in_22), .in1(29'h8881140), .in2(29'h8881fd0), .in3(29'h7000e00), .out(out_62), .sel(in_1));
  Multiplexer #(.select(2), .width(29), .enable("false")) multiplexer_30 (
    .in0(in_33), .in1(29'h8881120), .in2(29'h8880000), .in3({29{1'b0}}), .out(out_63), .sel(in_1));
  Multiplexer #(.select(2), .width(29), .enable("false")) multiplexer_31 (
    .in0(in_12), .in1(29'h8880e10), .in2(29'h8881fd0), .in3({29{1'b0}}), .out(out_64), .sel(in_1));
  Multiplexer #(.select(2), .width(29), .enable("false")) multiplexer_32 (
    .in0(in_23), .in1({29{1'b0}}), .in2({29{1'b0}}), .in3({29{1'b0}}), .out(out_65), .sel(in_1));

  // Other names for the same wires on the sheet: game_state[1:0] = in_1; in_1_t[28:0] = in_2; in_2_t[28:0] = in_13;
  //   in_3_t[28:0] = in_24; in_4_t[28:0] = in_3; in_5_t[28:0] = in_14; in_6_t[28:0] = in_25; in_7_t[28:0] = in_4;
  //   in_8_t[28:0] = in_15; in_9_t[28:0] = in_26; in_10_t[28:0] = in_5; in_11_t[28:0] = in_16; in_12_t[28:0] = in_27;
  //   in_13_t[28:0] = in_6; in_14_t[28:0] = in_17; in_15_t[28:0] = in_28; in_16_t[28:0] = in_7; in_17_t[28:0] = in_18;
  //   in_18_t[28:0] = in_29; in_19_t[28:0] = in_8; in_20_t[28:0] = in_19; in_21_t[28:0] = in_30; in_22_t[28:0] = in_9;
  //   in_23_t[28:0] = in_20; in_24_t[28:0] = in_31; in_25_t[28:0] = in_10; in_26_t[28:0] = in_21;
  //   in_27_t[28:0] = in_32; in_28_t[28:0] = in_11; in_29_t[28:0] = in_22; in_30_t[28:0] = in_33;
  //   in_31_t[28:0] = in_12; in_32_t[28:0] = in_23

  // Notes on the sheet:
  //   1
  //   3
  //   5
  //   7
  //   9
  //   11
  //   13
  //   15
  //   17
  //   19
  //   21
  //   23
  //   25
  //   27
  //   29
  //   31
endmodule

module COL_ADAPTER (
  input  [28:0] in_1,
  input  [28:0] in_2,
  input  [28:0] in_3,
  input  [28:0] in_4,
  input  [28:0] in_5,
  input  [28:0] in_6,
  input  [28:0] in_7,
  input  [28:0] in_8,
  input  [28:0] in_9,
  input  [28:0] in_10,
  input  [28:0] in_11,
  input  [28:0] in_12,
  input  [28:0] in_13,
  input  [28:0] in_14,
  input  [28:0] in_15,
  input  [28:0] in_16,
  input  [28:0] in_17,
  input  [28:0] in_18,
  input  [28:0] in_19,
  input  [28:0] in_20,
  input  [28:0] in_21,
  input  [28:0] in_22,
  input  [28:0] in_23,
  input  [28:0] in_24,
  input  [28:0] in_25,
  input  [28:0] in_26,
  input  [28:0] in_27,
  input  [28:0] in_28,
  input  [28:0] in_29,
  input  [28:0] in_30,
  input  [28:0] in_31,
  input  [28:0] in_32,
  input  [1:0] load
);

  GAME_SCREEN game_screen_1 (
    .in_1(load), .in_2(in_1), .in_3(in_7), .in_4(in_13), .in_5(in_18), .in_6(in_23), .in_7(in_28),
    .in_8(in_2), .in_9(in_8), .in_10(in_14), .in_11(in_19), .in_12(in_24), .in_13(in_29), .in_14(in_3),
    .in_15(in_9), .in_16(in_15), .in_17(in_20), .in_18(in_25), .in_19(in_30), .in_20(in_4), .in_21(in_10),
    .in_22(in_16), .in_23(in_21), .in_24(in_26), .in_25(in_31), .in_26(in_5), .in_27(in_11), .in_28(in_17),
    .in_29(in_22), .in_30(in_27), .in_31(in_32), .in_32(in_6), .in_33(in_12));  // open: out_34, out_35, out_36, out_37, out_38, out_39, out_40, out_41, out_42, out_43, out_44, out_45, out_46, out_47, out_48, out_49, out_50, out_51, out_52, out_53, out_54, out_55, out_56, out_57, out_58, out_59, out_60, out_61, out_62, out_63, out_64, out_65
  Subtractor subtractor_1 ();  // open: a, b, out, bin, bout

  // Other names for the same wires on the sheet: in_2_t[28:0] = in_7; in_3_t[28:0] = in_13; in_4_t[28:0] = in_18;
  //   in_5_t[28:0] = in_23; in_6_t[28:0] = in_28; in_7_t[28:0] = in_2; in_9_t[28:0] = in_14; in_10_t[28:0] = in_19;
  //   in_11_t[28:0] = in_24; in_12_t[28:0] = in_29; in_13_t[28:0] = in_3; in_14_t[28:0] = in_9; in_16_t[28:0] = in_20;
  //   in_17_t[28:0] = in_25; in_18_t[28:0] = in_30; in_19_t[28:0] = in_4; in_20_t[28:0] = in_10;
  //   in_21_t[28:0] = in_16; in_22_t[28:0] = in_21; in_23_t[28:0] = in_26; in_24_t[28:0] = in_31;
  //   in_25_t[28:0] = in_5; in_26_t[28:0] = in_11; in_27_t[28:0] = in_17; in_28_t[28:0] = in_22;
  //   in_29_t[28:0] = in_27; in_30_t[28:0] = in_32; in_31_t[28:0] = in_6; in_32_t[28:0] = in_12
endmodule

module DISPLAY_1 (
  input  [5:0] X,
  input  [4:0] Y,
  input  [7:0] in_3,
  input  in_4
);

  wire _0, _1_t, _2_t, _3_t, _4_t, _5_t, _6_t, _7_t, _8_t, _9_t, _10_t, _11_t, _12_t, _13_t, _14_t, _15_t,
       _16_t, _17_t, _18_t, _19_t, _20_t, _21_t, _22_t, _23_t, _24_t, _25_t, _26_t, _27_t, _28_t, _29_t,
       _30_t, _31_t, clock_1_out, clock_2_out, clock_3_out, clock_4_out, clock_5_out, decoder_1_out0,
       decoder_1_out1, decoder_1_out2, decoder_1_out3, decoder_1_out4, decoder_1_out5, decoder_1_out6,
       decoder_1_out7, decoder_1_out8, decoder_1_out9, decoder_1_out10, decoder_1_out11, decoder_1_out12,
       decoder_1_out13, decoder_1_out14, decoder_1_out15, decoder_1_out16, decoder_1_out17, decoder_1_out18,
       decoder_1_out19, decoder_1_out20, decoder_1_out21, decoder_1_out22, decoder_1_out23, decoder_1_out24,
       decoder_1_out25, decoder_1_out26, decoder_1_out27, decoder_1_out28, decoder_1_out29, decoder_1_out30,
       decoder_1_out31, not_1_out, not_2_out, not_3_out, not_4_out, not_5_out, not_6_out, not_7_out,
       not_8_out, not_9_out, not_10_out, not_11_out, not_12_out, not_13_out, not_14_out, not_15_out,
       not_16_out, not_17_out, not_18_out, not_19_out, not_20_out, not_21_out, not_22_out, not_23_out,
       not_24_out, not_25_out, not_26_out, not_27_out, not_28_out, not_29_out, not_30_out, not_31_out,
       not_32_out;
  wire [4:0] counter_1_q, register_3_q;
  wire [7:0] ram_1_data;
  wire [31:0] _1, _2, _3, _4, _5, _6, _7, _8, _9, _10, _11, _12, _13, _14, _15, _16, _17, _18, _19, _20, _21,
       _22, _23, _24, _25, _26, _27, _28, _29, _30, _31, _32, comparator_33_eq, register_32_q, register_33_q,
       register_34_q, register_35_q, register_36_q, register_37_q, register_38_q, register_39_q,
       register_40_q, register_41_q, register_42_q, register_43_q, register_44_q, register_45_q,
       register_46_q, register_47_q, register_48_q, register_49_q, register_50_q, register_51_q,
       register_52_q, register_53_q, register_54_q, register_55_q, register_56_q, register_57_q,
       register_58_q, register_59_q, register_60_q, register_61_q, register_62_q, register_65_q, rom_3_data;

  Register #(.width(6)) register_1 (.D(X), .clk(clock_1_out));  // open: en, Q, clr
  Clock clock_1 (.out(clock_1_out));
  Comparator #(.width(6), .mode("unsigned")) comparator_1 (.a(X), .b({6{1'b0}}), .eq(_0));  // open: gt, lt
  Comparator #(.width(6)) comparator_2 (.a(X), .b(6'b000001), .eq(_1_t));  // open: gt, lt
  Comparator #(.width(6)) comparator_3 (.a(X), .b(6'b000010), .eq(_2_t));  // open: gt, lt
  Comparator #(.width(6)) comparator_4 (.a(X), .b(6'b000011), .eq(_3_t));  // open: gt, lt
  Comparator #(.width(6)) comparator_5 (.a(X), .b(6'b000100), .eq(_4_t));  // open: gt, lt
  Comparator #(.width(6)) comparator_6 (.a(X), .b(6'b000101), .eq(_5_t));  // open: gt, lt
  Comparator #(.width(6)) comparator_7 (.a(X), .b(6'b000110), .eq(_6_t));  // open: gt, lt
  Comparator #(.width(6)) comparator_8 (.a(X), .b(6'b000111), .eq(_7_t));  // open: gt, lt
  Comparator #(.width(6)) comparator_9 (.a(X), .b(6'b001000), .eq(_8_t));  // open: gt, lt
  Comparator #(.width(6)) comparator_10 (.a(X), .b(6'b001001), .eq(_9_t));  // open: gt, lt
  Comparator #(.width(6)) comparator_11 (.a(X), .b(6'b001010), .eq(_10_t));  // open: gt, lt
  Comparator #(.width(6)) comparator_12 (.a(X), .b(6'b001011), .eq(_11_t));  // open: gt, lt
  Comparator #(.width(6)) comparator_13 (.a(X), .b(6'b001100), .eq(_12_t));  // open: gt, lt
  Comparator #(.width(6)) comparator_14 (.a(X), .b(6'b001101), .eq(_13_t));  // open: gt, lt
  Comparator #(.width(6)) comparator_15 (.a(X), .b(6'b001110), .eq(_14_t));  // open: gt, lt
  Comparator #(.width(6)) comparator_16 (.a(X), .b(6'b001111), .eq(_15_t));  // open: gt, lt
  Comparator #(.width(6)) comparator_17 (.a(X), .b(6'b010000), .eq(_16_t));  // open: gt, lt
  Comparator #(.width(6)) comparator_18 (.a(X), .b(6'b010001), .eq(_17_t));  // open: gt, lt
  Comparator #(.width(6)) comparator_19 (.a(X), .b(6'b010010), .eq(_18_t));  // open: gt, lt
  Comparator #(.width(6)) comparator_20 (.a(X), .b(6'b010011), .eq(_19_t));  // open: gt, lt
  Comparator #(.width(6)) comparator_21 (.a(X), .b(6'b010100), .eq(_20_t));  // open: gt, lt
  Comparator #(.width(6)) comparator_22 (.a(X), .b(6'b010101), .eq(_21_t));  // open: gt, lt
  Comparator #(.width(6)) comparator_23 (.a(X), .b(6'b010110), .eq(_22_t));  // open: gt, lt
  Comparator #(.width(6)) comparator_24 (.a(X), .b(6'b010111), .eq(_23_t));  // open: gt, lt
  Comparator #(.width(6)) comparator_25 (.a(X), .b(6'b011000), .eq(_24_t));  // open: gt, lt
  Comparator #(.width(6)) comparator_26 (.a(X), .b(6'b011001), .eq(_25_t));  // open: gt, lt
  Comparator #(.width(6)) comparator_27 (.a(X), .b(6'b011010), .eq(_26_t));  // open: gt, lt
  Comparator #(.width(6)) comparator_28 (.a(X), .b(6'b011011), .eq(_27_t));  // open: gt, lt
  Comparator #(.width(6)) comparator_29 (.a(X), .b(6'b011100), .eq(_28_t));  // open: gt, lt
  Comparator #(.width(6)) comparator_30 (.a(X), .b(6'b011101), .eq(_29_t));  // open: gt, lt
  Comparator #(.width(6)) comparator_31 (.a(X), .b(6'b011110), .eq(_30_t));  // open: gt, lt
  Comparator #(.width(6)) comparator_32 (.a(X), .b(6'b011111), .eq(_31_t));  // open: gt, lt
  Clock clock_2 (.out(clock_2_out));
  Register #(.width(32)) register_2 (.D(comparator_33_eq), .Q(_1), .clk(clock_2_out), .clr(not_1_out));  // open: en
  not not_1 (not_1_out, _0);
  Register #(.width(5)) register_3 (.D(Y), .Q(register_3_q), .clk(clock_3_out));  // open: en, clr
  Clock clock_3 (.out(clock_3_out));
  ROM #(.dataWidth(1)) rom_1 ();  // open: addr, data, sel
  Register #(.width(32)) register_4 (.D(comparator_33_eq), .Q(_2), .clk(clock_2_out), .clr(not_2_out));  // open: en
  not not_2 (not_2_out, _1_t);
  not not_3 (not_3_out, _2_t);
  Register #(.width(32)) register_5 (.D(comparator_33_eq), .Q(_3), .clk(clock_2_out), .clr(not_3_out));  // open: en
  Register #(.width(32)) register_6 (.D(comparator_33_eq), .Q(_4), .clk(clock_2_out), .clr(not_4_out));  // open: en
  not not_4 (not_4_out, _3_t);
  Comparator #(.width(5), .mode("unsigned")) comparator_33 (
    .a({5{1'b0}}), .b(register_3_q), .eq(comparator_33_eq[0]));  // open: gt, lt
  Comparator #(.width(5)) comparator_34 (.a(5'b00001), .b(register_3_q), .eq(comparator_33_eq[1]));  // open: gt, lt
  Comparator #(.width(5)) comparator_35 (.a(5'b00010), .b(register_3_q), .eq(comparator_33_eq[2]));  // open: gt, lt
  Comparator #(.width(5)) comparator_36 (.a(5'b00011), .b(register_3_q), .eq(comparator_33_eq[3]));  // open: gt, lt
  Comparator #(.width(5)) comparator_37 (.a(5'b00100), .b(register_3_q), .eq(comparator_33_eq[4]));  // open: gt, lt
  Comparator #(.width(5)) comparator_38 (.a(5'b00101), .b(register_3_q), .eq(comparator_33_eq[5]));  // open: gt, lt
  Comparator #(.width(5)) comparator_39 (.a(5'b00110), .b(register_3_q), .eq(comparator_33_eq[6]));  // open: gt, lt
  Comparator #(.width(5)) comparator_40 (.a(5'b00111), .b(register_3_q), .eq(comparator_33_eq[7]));  // open: gt, lt
  Comparator #(.width(5), .mode("unsigned")) comparator_41 (
    .a(5'b01000), .b(register_3_q), .eq(comparator_33_eq[8]));  // open: gt, lt
  Comparator #(.width(5)) comparator_42 (.a(5'b01001), .b(register_3_q), .eq(comparator_33_eq[9]));  // open: gt, lt
  Comparator #(.width(5)) comparator_43 (.a(5'b01010), .b(register_3_q), .eq(comparator_33_eq[10]));  // open: gt, lt
  Comparator #(.width(5)) comparator_44 (.a(5'b01011), .b(register_3_q), .eq(comparator_33_eq[11]));  // open: gt, lt
  Comparator #(.width(5)) comparator_45 (.a(5'b01100), .b(register_3_q), .eq(comparator_33_eq[12]));  // open: gt, lt
  Comparator #(.width(5)) comparator_46 (.a(5'b01101), .b(register_3_q), .eq(comparator_33_eq[13]));  // open: gt, lt
  Comparator #(.width(5)) comparator_47 (.a(5'b01110), .b(register_3_q), .eq(comparator_33_eq[14]));  // open: gt, lt
  Comparator #(.width(5)) comparator_48 (.a(5'b01111), .b(register_3_q), .eq(comparator_33_eq[15]));  // open: gt, lt
  Comparator #(.width(5)) comparator_49 (.a(5'b10000), .b(register_3_q), .eq(comparator_33_eq[16]));  // open: gt, lt
  Comparator #(.width(5)) comparator_50 (.a(5'b10001), .b(register_3_q), .eq(comparator_33_eq[17]));  // open: gt, lt
  Comparator #(.width(5)) comparator_51 (.a(5'b10010), .b(register_3_q), .eq(comparator_33_eq[18]));  // open: gt, lt
  Comparator #(.width(5)) comparator_52 (.a(5'b10011), .b(register_3_q), .eq(comparator_33_eq[19]));  // open: gt, lt
  Comparator #(.width(5)) comparator_53 (.a(5'b10100), .b(register_3_q), .eq(comparator_33_eq[20]));  // open: gt, lt
  Comparator #(.width(5)) comparator_54 (.a(5'b10101), .b(register_3_q), .eq(comparator_33_eq[21]));  // open: gt, lt
  Comparator #(.width(5), .mode("unsigned")) comparator_55 (
    .a(5'b10110), .b(register_3_q), .eq(comparator_33_eq[22]));  // open: gt, lt
  Comparator #(.width(5)) comparator_56 (.a(5'b10111), .b(register_3_q), .eq(comparator_33_eq[23]));  // open: gt, lt
  Comparator #(.width(5)) comparator_57 (.a(5'b11000), .b(register_3_q), .eq(comparator_33_eq[24]));  // open: gt, lt
  Comparator #(.width(5)) comparator_58 (.a(5'b11001), .b(register_3_q), .eq(comparator_33_eq[25]));  // open: gt, lt
  Comparator #(.width(5)) comparator_59 (.a(5'b11010), .b(register_3_q), .eq(comparator_33_eq[26]));  // open: gt, lt
  Comparator #(.width(5)) comparator_60 (.a(5'b11011), .b(register_3_q), .eq(comparator_33_eq[27]));  // open: gt, lt
  Comparator #(.width(5)) comparator_61 (.a(5'b11100), .b(register_3_q), .eq(comparator_33_eq[28]));  // open: gt, lt
  Comparator #(.width(5)) comparator_62 (.a(5'b11101), .b(register_3_q), .eq(comparator_33_eq[29]));  // open: gt, lt
  Comparator #(.width(5)) comparator_63 (.a(5'b11110), .b(register_3_q), .eq(comparator_33_eq[30]));  // open: gt, lt
  Comparator #(.width(5)) comparator_64 (.a({5{1'b1}}), .b(register_3_q), .eq(comparator_33_eq[31]));  // open: gt, lt
  Register #(.width(32)) register_7 (.D(comparator_33_eq), .Q(_5), .clk(clock_2_out), .clr(not_5_out));  // open: en
  not not_5 (not_5_out, _4_t);
  Register #(.width(32)) register_8 (.D(comparator_33_eq), .Q(_6), .clk(clock_2_out), .clr(not_6_out));  // open: en
  Register #(.width(32)) register_9 (.D(comparator_33_eq), .Q(_7), .clk(clock_2_out), .clr(not_7_out));  // open: en
  not not_6 (not_6_out, _5_t);
  not not_7 (not_7_out, _6_t);
  Register #(.width(32)) register_10 (.D(comparator_33_eq), .Q(_8), .clk(clock_2_out), .clr(not_8_out));  // open: en
  not not_8 (not_8_out, _7_t);
  Register #(.width(32)) register_11 (.D(comparator_33_eq), .Q(_9), .clk(clock_2_out), .clr(not_9_out));  // open: en
  not not_9 (not_9_out, _8_t);
  Register #(.width(32)) register_12 (.D(comparator_33_eq), .Q(_10), .clk(clock_2_out), .clr(not_10_out));  // open: en
  not not_10 (not_10_out, _9_t);
  Register #(.width(32)) register_13 (.D(comparator_33_eq), .Q(_11), .clk(clock_2_out), .clr(not_11_out));  // open: en
  not not_11 (not_11_out, _10_t);
  not not_12 (not_12_out, _11_t);
  Register #(.width(32)) register_14 (.D(comparator_33_eq), .Q(_13), .clk(clock_2_out), .clr(not_13_out));  // open: en
  Register #(.width(32)) register_15 (.D(comparator_33_eq), .Q(_12), .clk(clock_2_out), .clr(not_12_out));  // open: en
  not not_13 (not_13_out, _12_t);
  DotMatrix #(.matrixcols(32), .matrixrows(32)) dotmatrix_1 (
    .col0(_1), .col1(_2), .col2(_3), .col3(_4), .col4(_5), .col5(_6), .col6(_7), .col7(_8), .col8(_9),
    .col9(_10), .col10(_11), .col11(_12), .col12(_13), .col13(_14), .col14(_15), .col15(_16), .col16(_17),
    .col17(_18), .col18(_19), .col19(_20), .col20(_21), .col21(_22), .col22(_23), .col23(_24), .col24(_25),
    .col25(_26), .col26(_27), .col27(_28), .col28(_29), .col29(_30), .col30(_31), .col31(_32));
  Register #(.width(32)) register_16 (.D(comparator_33_eq), .Q(_14), .clk(clock_2_out), .clr(not_14_out));  // open: en
  not not_14 (not_14_out, _13_t);
  Register #(.width(32)) register_17 (.D(comparator_33_eq), .Q(_15), .clk(clock_2_out), .clr(not_16_out));  // open: en
  Register #(.width(32)) register_18 (.D(comparator_33_eq), .Q(_16), .clk(clock_2_out), .clr(not_15_out));  // open: en
  not not_15 (not_15_out, _15_t);
  not not_16 (not_16_out, _14_t);
  ROM #(.addrWidth(6), .dataWidth(32)) rom_2 ();  // open: addr, data, sel
  Register #(.width(32)) register_19 (.D(comparator_33_eq), .Q(_17), .clk(clock_2_out), .clr(not_17_out));  // open: en
  Register #(.width(32)) register_20 (.D(comparator_33_eq), .Q(_18), .clk(clock_2_out), .clr(not_18_out));  // open: en
  not not_17 (not_17_out, _16_t);
  not not_18 (not_18_out, _17_t);
  Counter #(.width(5), .max('h1f)) counter_1 (.Q(counter_1_q), .clk(clock_4_out));  // open: load, D, count, carry, clr
  Clock clock_4 (.out(clock_4_out));
  Register #(.width(32)) register_21 (.D(comparator_33_eq), .Q(_19), .clk(clock_2_out), .clr(not_19_out));  // open: en
  not not_19 (not_19_out, _18_t);
  Register #(.width(32)) register_22 (.D(comparator_33_eq), .Q(_20), .clk(clock_2_out), .clr(not_21_out));  // open: en
  not not_20 (not_20_out, _20_t);
  not not_21 (not_21_out, _19_t);
  Register #(.width(32)) register_23 (.D(comparator_33_eq), .Q(_22), .clk(clock_2_out), .clr(not_22_out));  // open: en
  Register #(.width(32)) register_24 (.D(comparator_33_eq), .Q(_21), .clk(clock_2_out), .clr(not_20_out));  // open: en
  not not_22 (not_22_out, _21_t);
  ROM #(.addrWidth(6), .dataWidth(32)) rom_3 (.addr({in_4, counter_1_q}), .data(rom_3_data));  // open: sel
  Register #(.width(32)) register_25 (.D(comparator_33_eq), .Q(_23), .clk(clock_2_out), .clr(not_23_out));  // open: en
  not not_23 (not_23_out, _22_t);
  Decoder #(.select(5), .enable("false")) decoder_1 (
    .out0(decoder_1_out0), .out1(decoder_1_out1), .out2(decoder_1_out2), .out3(decoder_1_out3),
    .out4(decoder_1_out4), .out5(decoder_1_out5), .out6(decoder_1_out6), .out7(decoder_1_out7),
    .out8(decoder_1_out8), .out9(decoder_1_out9), .out10(decoder_1_out10), .out11(decoder_1_out11),
    .out12(decoder_1_out12), .out13(decoder_1_out13), .out14(decoder_1_out14), .out15(decoder_1_out15),
    .out16(decoder_1_out16), .out17(decoder_1_out17), .out18(decoder_1_out18), .out19(decoder_1_out19),
    .out20(decoder_1_out20), .out21(decoder_1_out21), .out22(decoder_1_out22), .out23(decoder_1_out23),
    .out24(decoder_1_out24), .out25(decoder_1_out25), .out26(decoder_1_out26), .out27(decoder_1_out27),
    .out28(decoder_1_out28), .out29(decoder_1_out29), .out30(decoder_1_out30), .out31(decoder_1_out31),
    .sel(counter_1_q));
  Register #(.width(32)) register_26 (.D(comparator_33_eq), .Q(_24), .clk(clock_2_out), .clr(not_24_out));  // open: en
  not not_24 (not_24_out, _23_t);
  Clock clock_5 (.out(clock_5_out));
  Register #(.width(32)) register_27 (.D(comparator_33_eq), .Q(_25), .clk(clock_2_out), .clr(not_25_out));  // open: en
  not not_25 (not_25_out, _24_t);
  RAM ram_1 (.addr(in_3), .data(ram_1_data), .clk(clock_5_out));  // open: sel, ld, clr
  Register #(.width(32)) register_28 (.D(comparator_33_eq), .Q(_26), .clk(clock_2_out), .clr(not_27_out));  // open: en
  Register #(.width(32)) register_29 (.D(comparator_33_eq), .Q(_27), .clk(clock_2_out), .clr(not_26_out));  // open: en
  not not_26 (not_26_out, _26_t);
  not not_27 (not_27_out, _25_t);
  Register #(.width(32)) register_30 (.D(comparator_33_eq), .Q(_28), .clk(clock_2_out), .clr(not_28_out));  // open: en
  not not_28 (not_28_out, _27_t);
  Counter #(.width(5), .max('h1f)) counter_2 (.clk(clock_5_out));  // open: load, D, count, Q, carry, clr
  Register #(.width(32)) register_31 (.D(comparator_33_eq), .Q(_29), .clk(clock_2_out), .clr(not_29_out));  // open: en
  not not_29 (not_29_out, _28_t);
  not not_30 (not_30_out, _29_t);
  Register #(.width(32)) register_32 (
    .D(rom_3_data), .en(decoder_1_out0), .Q(register_32_q), .clk(clock_5_out));  // open: clr
  Register #(.width(32)) register_33 (
    .D(rom_3_data), .en(decoder_1_out1), .Q(register_33_q), .clk(clock_5_out));  // open: clr
  Register #(.width(32)) register_34 (
    .D(rom_3_data), .en(decoder_1_out2), .Q(register_34_q), .clk(clock_5_out));  // open: clr
  Register #(.width(32)) register_35 (
    .D(rom_3_data), .en(decoder_1_out3), .Q(register_35_q), .clk(clock_5_out));  // open: clr
  Register #(.width(32)) register_36 (
    .D(rom_3_data), .en(decoder_1_out4), .Q(register_36_q), .clk(clock_5_out));  // open: clr
  Register #(.width(32)) register_37 (
    .D(rom_3_data), .en(decoder_1_out5), .Q(register_37_q), .clk(clock_5_out));  // open: clr
  Register #(.width(32)) register_38 (
    .D(rom_3_data), .en(decoder_1_out6), .Q(register_38_q), .clk(clock_5_out));  // open: clr
  Register #(.width(32)) register_39 (
    .D(rom_3_data), .en(decoder_1_out7), .Q(register_39_q), .clk(clock_5_out));  // open: clr
  Register #(.width(32)) register_40 (
    .D(rom_3_data), .en(decoder_1_out8), .Q(register_40_q), .clk(clock_5_out));  // open: clr
  Register #(.width(32)) register_41 (
    .D(rom_3_data), .en(decoder_1_out9), .Q(register_41_q), .clk(clock_5_out));  // open: clr
  Register #(.width(32)) register_42 (
    .D(rom_3_data), .en(decoder_1_out10), .Q(register_42_q), .clk(clock_5_out));  // open: clr
  Register #(.width(32)) register_43 (
    .D(rom_3_data), .en(decoder_1_out11), .Q(register_43_q), .clk(clock_5_out));  // open: clr
  Register #(.width(32)) register_44 (
    .D(rom_3_data), .en(decoder_1_out12), .Q(register_44_q), .clk(clock_5_out));  // open: clr
  Register #(.width(32)) register_45 (
    .D(rom_3_data), .en(decoder_1_out13), .Q(register_45_q), .clk(clock_5_out));  // open: clr
  Register #(.width(32)) register_46 (
    .D(rom_3_data), .en(decoder_1_out14), .Q(register_46_q), .clk(clock_5_out));  // open: clr
  Register #(.width(32)) register_47 (
    .D(rom_3_data), .en(decoder_1_out15), .Q(register_47_q), .clk(clock_5_out));  // open: clr
  Register #(.width(32)) register_48 (
    .D(rom_3_data), .en(decoder_1_out16), .Q(register_48_q), .clk(clock_5_out));  // open: clr
  Register #(.width(32)) register_49 (
    .D(rom_3_data), .en(decoder_1_out17), .Q(register_49_q), .clk(clock_5_out));  // open: clr
  Register #(.width(32)) register_50 (
    .D(rom_3_data), .en(decoder_1_out18), .Q(register_50_q), .clk(clock_5_out));  // open: clr
  Register #(.width(32)) register_51 (
    .D(rom_3_data), .en(decoder_1_out19), .Q(register_51_q), .clk(clock_5_out));  // open: clr
  Register #(.width(32)) register_52 (
    .D(rom_3_data), .en(decoder_1_out20), .Q(register_52_q), .clk(clock_5_out));  // open: clr
  Register #(.width(32)) register_53 (
    .D(rom_3_data), .en(decoder_1_out21), .Q(register_53_q), .clk(clock_5_out));  // open: clr
  Register #(.width(32)) register_54 (
    .D(rom_3_data), .en(decoder_1_out22), .Q(register_54_q), .clk(clock_5_out));  // open: clr
  Register #(.width(32)) register_55 (
    .D(rom_3_data), .en(decoder_1_out23), .Q(register_55_q), .clk(clock_5_out));  // open: clr
  Register #(.width(32)) register_56 (
    .D(rom_3_data), .en(decoder_1_out24), .Q(register_56_q), .clk(clock_5_out));  // open: clr
  Register #(.width(32)) register_57 (
    .D(rom_3_data), .en(decoder_1_out25), .Q(register_57_q), .clk(clock_5_out));  // open: clr
  Register #(.width(32)) register_58 (
    .D(rom_3_data), .en(decoder_1_out27), .Q(register_58_q), .clk(clock_5_out));  // open: clr
  Register #(.width(32)) register_59 (
    .D(rom_3_data), .en(decoder_1_out28), .Q(register_59_q), .clk(clock_5_out));  // open: clr
  Register #(.width(32)) register_60 (
    .D(rom_3_data), .en(decoder_1_out29), .Q(register_60_q), .clk(clock_5_out));  // open: clr
  Register #(.width(32)) register_61 (
    .D(rom_3_data), .en(decoder_1_out30), .Q(register_61_q), .clk(clock_5_out));  // open: clr
  Register #(.width(32)) register_62 (
    .D(rom_3_data), .en(decoder_1_out31), .Q(register_62_q), .clk(clock_5_out));  // open: clr
  Register #(.width(32)) register_63 (.D(comparator_33_eq), .Q(_30), .clk(clock_2_out), .clr(not_30_out));  // open: en
  Register #(.width(32)) register_64 (.D(comparator_33_eq), .Q(_31), .clk(clock_2_out), .clr(not_31_out));  // open: en
  not not_31 (not_31_out, _30_t);
  Register #(.width(32)) register_65 (
    .D(rom_3_data), .en(decoder_1_out26), .Q(register_65_q), .clk(clock_5_out));  // open: clr
  Register #(.width(32)) register_66 (.D(comparator_33_eq), .Q(_32), .clk(clock_2_out), .clr(not_32_out));  // open: en
  not not_32 (not_32_out, _31_t);
  DotMatrix #(.matrixcols(32), .matrixrows(32)) dotmatrix_2 (
    .col0(register_32_q), .col1(register_33_q), .col2(register_34_q), .col3(register_35_q),
    .col4(register_36_q), .col5(register_37_q), .col6(register_38_q), .col7(register_39_q),
    .col8(register_40_q), .col9(register_41_q), .col10(register_42_q), .col11(register_43_q),
    .col12(register_44_q), .col13(register_45_q), .col14(register_46_q), .col15(register_47_q),
    .col16(register_48_q), .col17(register_49_q), .col18(register_50_q), .col19(register_51_q),
    .col20(register_52_q), .col21(register_53_q), .col22(register_54_q), .col23(register_55_q),
    .col24(register_56_q), .col25(register_57_q), .col26(register_65_q), .col27(register_58_q),
    .col28(register_59_q), .col29(register_60_q), .col30(register_61_q), .col31(register_62_q));

  // Notes on the sheet:
  //   contents of rom_2 (hex, n*v repeats v):
  //   1 12*80000001 8fffff01 7*80000001 87fffff1 6*84000001 80000001 80000001 80000001 ffffffff
  //   contents of rom_3 (hex, n*v repeats v):
  //   ffffffff 80000001 80000001 80000001 fffffff1 80000001 80000001 80000001 87fffff1 84000001 84000001
  //   84000001 84007c01 84004401 84004401 84004401 84007c01 84000001 84000001 84000001 87fffff1
  //   10*80000001 80000000 84007c01 84000001 84000001 84000001 87fffff1 10*80000001 80000000 84004401
  //   84004401 84007c01 84000001 84000001 84000001 87fffff1 8*80000001 ffffffff
endmodule
