// Logisim project PROJECT.circ as structural Verilog: 7 circuits, main circuit main
module main (
);

  wire DOWN_out, LEFT_out, RESET, RIGHT_out, TACTS, UP_out;
  wire [11:0] player_pos_1_addr;

  Clock clock_1 (.out(TACTS));
  Button UP (.out(UP_out));
  Button DOWN (.out(DOWN_out));
  Button LEFT (.out(LEFT_out));
  Button RIGHT (.out(RIGHT_out));
  Button u_RESET (.out(RESET));
  BTN_INPUT btn_input_1 (
    .TACT(TACTS), .RIGHT(UP_out), .LEFT(DOWN_out), .UP(LEFT_out), .DOWN(RIGHT_out), .RESET(RESET));  // open: B_RIGHT, B_LEFT, B_UP, B_DOWN, B_RESET
  MOVE_LOGIC move_logic_1 ();  // open: POS_Y, POS_X, POS_Y_2, POS_X_2, CELL_TYPE, MOVE_ENABLE, GAME_STATE, B_RIGHT, B_LEFT, B_UP, B_DOWN, NEW_Y_U, SAFE_U, SAFE_R, NEW_X_R, SAFE_D, NEW_Y_D, NEW_X_L, SAFE_L, IS_PASS, IS_WALL, IS_KEY, IS_EXIT_C, IS_EXIT_O, IS_TRAP, IS_BONUS, IS_START, RIGHT_OK, LEFT_OK, UP_OK, DOWN_OK
  PLAYER_POS player_pos_1 (
    .RESET(RESET), .in_2(RESET), .in_5(RESET), .in_3(TACTS), .in_6(TACTS), .ADDR(player_pos_1_addr));  // open: NEW_X, NEW_Y, LOAD_X, LOAD_Y, POS_X, POS_Y
  // MAP_MEM map_mem_1: pin names not known; wires that end beside it: player_pos_1_addr, TACTS
  DotMatrix #(.matrixcols(32), .matrixrows(32)) dotmatrix_1 ();  // open: col0, col1, col2, col3, col4, col5, col6, col7, col8, col9, col10, col11, col12, col13, col14, col15, col16, col17, col18, col19, col20, col21, col22, col23, col24, col25, col26, col27, col28, col29, col30, col31
endmodule

module BTN_INPUT (
  input  TACT,
  input  RIGHT,
  input  LEFT,
  input  UP,
  input  DOWN,
  input  RESET,
  output B_RIGHT,
  output B_LEFT,
  output B_UP,
  output B_DOWN,
  output B_RESET
);

  wire clock_1_out, d_ff_1_q, d_ff_2_q, d_ff_3_q, d_ff_4_q, not_1_out, not_2_out, not_3_out, not_4_out;

  Clock clock_1 (.out(clock_1_out));
  D_Flip_Flop d_ff_1 (.clk(clock_1_out), .D(RIGHT), .Q(d_ff_1_q));  // open: Qn, preset, en, reset
  D_Flip_Flop d_ff_2 (.clk(clock_1_out), .D(LEFT), .Q(d_ff_2_q));  // open: Qn, preset, en, reset
  D_Flip_Flop d_ff_3 (.clk(clock_1_out), .D(UP), .Q(d_ff_3_q));  // open: Qn, preset, en, reset
  D_Flip_Flop d_ff_4 (.clk(clock_1_out), .D(DOWN), .Q(d_ff_4_q));  // open: Qn, preset, en, reset
  not not_1 (not_1_out, d_ff_1_q);
  not not_2 (not_2_out, d_ff_2_q);
  not not_3 (not_3_out, d_ff_3_q);
  not not_4 (not_4_out, d_ff_4_q);
  and and_1 (B_RIGHT, not_1_out, RIGHT);
  and and_2 (B_LEFT, not_2_out, LEFT);
  and and_3 (B_UP, not_3_out, UP);
  and and_4 (B_DOWN, not_4_out, DOWN);

  assign B_RESET = RESET;
endmodule

module PLAYER_POS (
  input  [5:0] NEW_X,
  input  in_2,
  input  in_3,
  input  [5:0] NEW_Y,
  input  in_5,
  input  in_6,
  input  LOAD_X,
  input  RESET,
  input  LOAD_Y,
  output [5:0] POS_X,
  output [11:0] ADDR,
  output [5:0] POS_Y
);

  wire LOAD_X_OR_RESET, LOAD_Y_OR_RESET;
  wire [5:0] multiplexer_1_out, multiplexer_2_out;

  or or_1 (LOAD_X_OR_RESET, LOAD_X, RESET);
  or or_2 (LOAD_Y_OR_RESET, RESET, LOAD_Y);
  Multiplexer #(.width(6)) multiplexer_1 (
    .in0(NEW_X), .in1(6'b000010), .out(multiplexer_1_out), .sel(in_2));  // open: en
  Multiplexer #(.width(6)) multiplexer_2 (
    .in0(NEW_Y), .in1(6'b000010), .out(multiplexer_2_out), .sel(in_5));  // open: en
  Register #(.width(6)) u_POS_X (.D(multiplexer_1_out), .en(LOAD_X_OR_RESET), .Q(ADDR[5:0]), .clk(in_3));  // open: clr
  Register #(.width(6)) u_POS_Y (.D(multiplexer_2_out), .en(LOAD_Y_OR_RESET), .Q(ADDR[11:6]), .clk(in_6));  // open: clr

  assign POS_X = ADDR[5:0];
  assign POS_Y = ADDR[11:6];

  // Notes on the sheet:
  //   START_X
  //   START_Y
endmodule

module MAP_MEM (
  input  [11:0] ADDR,
  input  [11:0] ADDR_NEXT,
  input  WE,
  input  TACT,
  input  [11:0] ADDR_2,
  output [3:0] CELL_TYPE,
  output [3:0] SCAN_Q
);

  Multiplexer #(.width(12)) multiplexer_1 (.in0(ADDR_NEXT), .in1(ADDR_2));  // open: out, sel, en
  RAM #(.addrWidth(12), .dataWidth(4), .bus("separate")) ram_1 (
    .addr(ADDR), .din(4'b0000), .data(CELL_TYPE), .str(WE), .sel(1'b1), .clk(TACT), .ld(1'b1), .clr(1'b0));
  RAM #(.addrWidth(12), .dataWidth(4)) ram_2 ();  // open: addr, data, sel, clk, ld, clr
  Counter counter_1 ();  // open: load, D, count, Q, carry, clk, clr

  assign SCAN_Q = CELL_TYPE;

  // Notes on the sheet:
  //   MAP_DATA_BACKUP
  //   MAP_DATA
endmodule

module RESET (
  input  TACT
);
endmodule

module MOVE_LOGIC (
  input  [5:0] POS_Y,
  input  [5:0] POS_X,
  input  [5:0] POS_Y_2,
  input  [5:0] POS_X_2,
  input  [3:0] CELL_TYPE,
  input  MOVE_ENABLE,
  input  [1:0] GAME_STATE,
  input  B_RIGHT,
  input  B_LEFT,
  input  B_UP,
  input  B_DOWN,
  output [5:0] NEW_Y_U,
  output SAFE_U,
  output SAFE_R,
  output [5:0] NEW_X_R,
  output SAFE_D,
  output [5:0] NEW_Y_D,
  output [5:0] NEW_X_L,
  output SAFE_L,
  output IS_PASS,
  output IS_WALL,
  output IS_KEY,
  output IS_EXIT_C,
  output IS_EXIT_O,
  output IS_TRAP,
  output IS_BONUS,
  output IS_START,
  output RIGHT_OK,
  output LEFT_OK,
  output UP_OK,
  output DOWN_OK
);

  wire ALLOWED, comparator_2_eq, comparator_3_gt, comparator_4_gt, comparator_5_eq, GANE_ACTIVE, not_1_out;

  Adder #(.width(6)) adder_1 (.a(POS_Y), .b(6'b000001), .out(NEW_Y_U));  // open: cin, cout
  Adder #(.width(6)) adder_2 (.a(POS_X), .b({6{1'b0}}), .out(NEW_X_R));  // open: cin, cout
  Subtractor #(.width(6)) subtractor_1 (.a(POS_Y_2), .b(6'b111110), .out(NEW_Y_D));  // open: bin, bout
  Subtractor #(.width(6)) subtractor_2 (.a(POS_X_2), .b({6{1'b0}}), .out(NEW_X_L));  // open: bin, bout
  Comparator #(.width(2)) comparator_1 (.a(GAME_STATE), .b(2'b00), .eq(GANE_ACTIVE));  // open: gt, lt
  Comparator #(.width(6), .mode("unsigned")) comparator_2 (
    .a(POS_Y), .b({6{1'b0}}), .eq(comparator_2_eq));  // open: gt, lt
  Comparator #(.width(6), .mode("unsigned")) comparator_3 (
    .a(NEW_X_R), .b(6'b111110), .gt(comparator_3_gt));  // open: eq, lt
  Comparator #(.width(6), .mode("unsigned")) comparator_4 (
    .a(NEW_Y_D), .b({6{1'b0}}), .gt(comparator_4_gt));  // open: eq, lt
  Comparator #(.width(6), .mode("unsigned")) comparator_5 (
    .a(POS_X_2), .b({6{1'b0}}), .eq(comparator_5_eq));  // open: gt, lt
  Decoder #(.select(4)) decoder_1 (
    .out0(IS_PASS), .out1(IS_WALL), .out2(IS_KEY), .out3(IS_EXIT_C), .out4(IS_EXIT_O), .out5(IS_TRAP),
    .out6(IS_BONUS), .out7(IS_START), .sel(CELL_TYPE));  // open: out8, out9, out10, out11, out12, out13, out14, out15, en
  not not_1 (not_1_out, comparator_5_eq);
  not not_2 (SAFE_U, comparator_2_eq);
  not not_3 (SAFE_R, comparator_3_gt);
  not not_4 (SAFE_D, comparator_4_gt);
  not not_5 (SAFE_L, not_1_out);
  and and_1 (ALLOWED, GANE_ACTIVE, MOVE_ENABLE);
  and and_2 (RIGHT_OK, B_RIGHT, MOVE_ENABLE);
  and and_3 (LEFT_OK, B_LEFT, MOVE_ENABLE);
  and and_4 (UP_OK, B_UP, MOVE_ENABLE);
  and and_5 (DOWN_OK, B_DOWN, MOVE_ENABLE);

  // Notes on the sheet:
  //   UP
  //   RIGHT
  //   DOWN
  //   LEFT
endmodule

module DISPLAY (
  input  [5:0] POS_X,
  input  [5:0] POS_Y,
  input  TACT,
  input  [3:0] MAP_Q,
  output [11:0] SCAN_ADDR
);

  wire and_1_out, comparator_1_eq, comparator_2_eq, decoder_1_out0, decoder_1_out1, decoder_1_out2,
       decoder_1_out3, decoder_1_out4, decoder_1_out5, decoder_1_out6, SCAN_X_carry;

  Counter #(.width(6), .max('h3f)) SCAN_X (
    .Q(SCAN_ADDR[5:0]), .carry(SCAN_X_carry), .clk(TACT));  // open: load, D, count, clr
  Counter #(.width(6), .max('h3f)) SCAN_y (
    .Q(SCAN_ADDR[11:6]), .clk(SCAN_X_carry));  // open: load, D, count, carry, clr
  Decoder #(.select(4)) decoder_1 (
    .out0(decoder_1_out0), .out1(decoder_1_out1), .out2(decoder_1_out2), .out3(decoder_1_out3),
    .out4(decoder_1_out4), .out5(decoder_1_out5), .out6(decoder_1_out6), .sel(MAP_Q));  // open: out7, out8, out9, out10, out11, out12, out13, out14, out15, en
  Comparator #(.width(6)) comparator_1 (.a(SCAN_ADDR[5:0]), .b(POS_X), .eq(comparator_1_eq));  // open: gt, lt
  Comparator #(.width(6)) comparator_2 (.a(SCAN_ADDR[11:6]), .b(POS_Y), .eq(comparator_2_eq));  // open: gt, lt
  and and_1 (and_1_out, comparator_1_eq, comparator_2_eq);
  // OR_Gate or_1 has open pins: in0=decoder_1_out0, in1=decoder_1_out1, in2=decoder_1_out2, in3=decoder_1_out3, in4=decoder_1_out4, in5=decoder_1_out5, in6=decoder_1_out6, out=open
endmodule
